# Fritzing sketch boeing 737-800 (saved by Fritzing 0.9.3b)
breadboards: 6

parts:
  Часть1 = Arduino Nano (Rev3.0)
  StrobeR = LED - 3mm [color="White (6500K)" package="3 mm [THT]"]
  STED_WR = LED - 3mm [color="White (6500K)" package="3 mm [THT]"]
  STED_GR = LED - 3mm [color="Green (570nm)" package="3 mm [THT]"]
  STED_WL = LED - 3mm [color="White (6500K)" package="3 mm [THT]"]
  StrobeL = LED - 3mm [color="White (6500K)" package="3 mm [THT]"]
  STED_RL = LED - 3mm [color="Red (660nm)" package="3 mm [THT]"]
  StrobeC = LED - 3mm [color="White (6500K)" package="3 mm [THT]"]
  STED_WC = LED - 3mm [color="White (6500K)" package="3 mm [THT]"]
  IL0 = LED - 3mm [color="White (6500K)" package="3 mm [THT]"]
  IL1 = LED - 3mm [color="White (6500K)" package="3 mm [THT]"]
  AC_2 = LED - 3mm [color="Red (660nm)" package="3 mm [THT]"]
  LandR = LED - 3mm [color="White (6500K)" package="3 mm [THT]"]
  LandC = LED - 3mm [color="White (6500K)" package="3 mm [THT]"]
  AC_1 = LED - 3mm [color="Red (660nm)" package="3 mm [THT]"]
  DFPlayer_Mini1 = DFPlayer MINI [package="DIP (Dual Inline) [THT]"]  # not connected
  U1 = Mini-360 DC-DC Buck converter [package=THT]
  LandL = LED - 3mm [color="White (6500K)" package="3 mm [THT]"]
  S1 = Square Pushbutton
  M1 = hcmmodu0083 [package=THT]
  VCC1 = Battery block 9V
  M2 = hcmmodu0083 [package=THT]
  R1 = Resistor [tolerance=±5% resistance=220 package=THT]
  R2 = Resistor [tolerance=±5% resistance=220 package=THT]
  R3 = Resistor [tolerance=±5% resistance=220 package=THT]
  R4 = Resistor [tolerance=±5% resistance=220 package=THT]
  R5 = Resistor [tolerance=±5% resistance=220 package=THT]
  R6 = Resistor [tolerance=±5% resistance=220 package=THT]
  R7 = Resistor [tolerance=±5% resistance=220 package=THT]
  R1_2 = Resistor [tolerance=±5% resistance=220 package=THT]
  R9 = Resistor [tolerance=±5% resistance=220 package=THT]
  IL2 = LED - 3mm [color="White (6500K)" package="3 mm [THT]"]
  IL3 = LED - 3mm [color="White (6500K)" package="3 mm [THT]"]
  R10 = Resistor [tolerance=±5% resistance=220 package=THT]
  R11 = Resistor [tolerance=±5% resistance=220 package=THT]
  S3 = Square Pushbutton

nets:
  N1: Часть1.GND, StrobeR.cathode, StrobeL.cathode, StrobeC.cathode, U1.IN-, M1.pin6, M2.pin3, R9.Pin_0
  N2: Часть1.D2, M1.pin1
  N3: Часть1.D3, M2.pin1
  N4: Часть1.D7, R2.Pin_1, R4.Pin_1
  N5: Часть1.D8, R6.Pin_1
  N6: Часть1.D10, AC_2.anode
  N7: Часть1.D11/MOSI, AC_1.anode
  N8: Часть1.VIN, U1.IN+, S1.leg1, M1.pin7
  N9: StrobeR.anode, R2.Pin_0
  N10: STED_WR.cathode, STED_GR.anode
  N11: STED_WR.anode, R1.Pin_0
  N12: STED_GR.cathode, STED_RL.cathode, STED_WC.cathode, IL0.cathode, LandR.cathode, LandC.cathode, M2.pin6, IL2.cathode
  N13: STED_WL.cathode, STED_RL.anode
  N14: STED_WL.anode, R3.Pin_0
  N15: StrobeL.anode, R4.Pin_0
  N16: StrobeC.anode, R6.Pin_0
  N17: STED_WC.anode, R5.Pin_0
  N18: IL0.anode, IL1.cathode
  N19: IL1.anode, R10.Pin_0
  N20: AC_2.cathode, AC_1.cathode, R9.Pin_1
  N21: LandR.anode, LandL.cathode
  N22: LandC.anode, R7.Pin_0
  N23: U1.OUT+, M2.pin5
  N24: U1.OUT-, M2.pin4
  N25: LandL.anode, R1_2.Pin_0
  N26: S1.leg0, M1.pin5, S3.leg1
  N27: M1.pin4, VCC1.-
  N28: VCC1.+, S3.leg0
  N29: M2.pin7, R1.Pin_1, R3.Pin_1, R5.Pin_1, R7.Pin_1, R1_2.Pin_1, R10.Pin_1, R11.Pin_1
  N30: IL2.anode, IL3.cathode
  N31: IL3.anode, R11.Pin_0

custom parts:
  DFPlayer MINI: MP3 module by DFRobot.com for playing Music from an SD-Card. Supports WAV and MP3 files.
  Mini-360 DC-DC Buck converter: Mini-360 DC-DC Buck converter. Tiny buck step down voltage converter, input voltage 4.75 to 23V output 1 to 17V adjustable. Available from ebay and the like.
  hcmmodu0083: hcmmodu0083 IRF540 Mosfet driver module
